# Fritzing sketch Sketch (saved by Fritzing 0.9.3b)
breadboards: 1

parts:
  Part1 = Arduino Uno (Rev3)
  LED1 = LED - 5mm [color="Red (633nm)" package="5 mm [THT]"]
  pH_Circuit1 = pH Circuit  # not connected
  D_O_Circuit1 = D.O. Circuit  # not connected
  L1 = Solenoid  # not connected
  S1 = Pushbutton [package="[THT]"]  # not connected
  S2 = Pushbutton [package="[THT]"]  # not connected

nets:
  N1: Part1.D13/SCK, LED1.anode
  N2: Part1.GND, LED1.cathode
